// Logisim project 13363476-Ass4C.circ as structural Verilog: 4 circuits, main circuit main
module main (
  input  [7:0] DataIn,
  input  [7:0] Address,
  input  WriteControl,
  input  Reset,
  output out_5,
  output out_6,
  output out_7,
  output out_8,
  output out_9,
  output out_10,
  output out_11,
  output out_12
);

  wire Clock_out, not_1_out;

  Clock Clock (.out(Clock_out));
  assign {out_12, out_11, out_10, out_9, out_8, out_7, out_6, out_5} = WriteControl ? DataIn : 8'bz;  // Controlled_Buffer Control_Buffer
  RAM #(.bus("asynch")) ram_1 (
    .addr(Address), .data({out_12, out_11, out_10, out_9, out_8, out_7, out_6, out_5}), .sel(1'b1),
    .ld(not_1_out), .clr(Reset));
  not not_1 (not_1_out, WriteControl);

  // Notes on the sheet:
  //   DataIn: pull=down
endmodule

module Q2 (
  input  [7:0] DataIn,
  input  [7:0] Address,
  input  [7:0] Offset,
  input  WriteControl,
  input  Reset,
  output out_6,
  output out_7,
  output out_8,
  output out_9,
  output out_10,
  output out_11,
  output out_12,
  output out_13
);

  wire not_1_out;
  wire [7:0] adder_1_out;

  Adder adder_1 (.a(Address), .b(Offset), .out(adder_1_out));  // open: cin, cout
  assign {out_13, out_12, out_11, out_10, out_9, out_8, out_7, out_6} = WriteControl ? DataIn : 8'bz;  // Controlled_Buffer Control_Buffer
  not not_1 (not_1_out, WriteControl);
  RAM #(.bus("asynch")) ram_1 (
    .addr(adder_1_out), .data({out_13, out_12, out_11, out_10, out_9, out_8, out_7, out_6}), .sel(1'b1),
    .ld(not_1_out), .clr(Reset));

  // Notes on the sheet:
  //   DataIn: pull=down
  //   Offset: pull=down
endmodule

module Q3 (
  input  [1:0] WriteReg,
  input  [1:0] ReadReg1,
  input  [1:0] ReadReg2,
  input  [7:0] Offset,
  input  RegWrite,
  input  WriteControl,
  input  Reset,
  output out_8,
  output out_9,
  output out_10,
  output out_11,
  output out_12,
  output out_13,
  output out_14,
  output out_15
);

  wire Clock_out, not_1_out;
  wire [7:0] adder_1_out, register_file_1_readdata1, register_file_1_readdata2;

  Clock Clock (.out(Clock_out));
  register_file register_file_1 (
    .WriteData({out_15, out_14, out_13, out_12, out_11, out_10, out_9, out_8}), .WriteReg(WriteReg),
    .RegWrite(RegWrite), .Clock(Clock_out), .ReadData1(register_file_1_readdata1), .ReadReg1(ReadReg1),
    .ReadData2(register_file_1_readdata2), .ReadReg2(ReadReg2));
  Adder adder_1 (.a(register_file_1_readdata1), .b(Offset), .out(adder_1_out));  // open: cin, cout
  assign {out_15, out_14, out_13, out_12, out_11, out_10, out_9, out_8} = WriteControl ? register_file_1_readdata2 : 8'bz;  // Controlled_Buffer Control_Buffer
  not not_1 (not_1_out, WriteControl);
  RAM #(.bus("asynch")) ram_1 (
    .addr(adder_1_out), .data({out_15, out_14, out_13, out_12, out_11, out_10, out_9, out_8}), .sel(1'b1),
    .ld(not_1_out), .clr(Reset));

  // Notes on the sheet:
  //   Offset: pull=down
endmodule

module register_file (
  input  [7:0] WriteData,
  input  [1:0] WriteReg,
  input  [1:0] ReadReg1,
  input  [1:0] ReadReg2,
  input  RegWrite,
  input  Clock,
  output [7:0] ReadData1,
  output [7:0] ReadData2
);

  wire and_1_out, and_2_out, and_3_out, and_4_out, decoder_1_out0, decoder_1_out1, decoder_1_out2,
       decoder_1_out3;
  wire [7:0] multiplexer_1_out, multiplexer_2_out, multiplexer_3_out, multiplexer_4_out, register_1_q,
       register_2_q, register_3_q, register_4_q;

  Decoder #(.select(2), .enable("false")) decoder_1 (
    .out0(decoder_1_out0), .out1(decoder_1_out1), .out2(decoder_1_out2), .out3(decoder_1_out3), .sel(WriteReg));
  and and_1 (and_1_out, decoder_1_out0, RegWrite);
  and and_2 (and_2_out, decoder_1_out1, RegWrite);
  and and_3 (and_3_out, decoder_1_out2, RegWrite);
  and and_4 (and_4_out, decoder_1_out3, RegWrite);
  Multiplexer #(.width(8), .enable("false")) multiplexer_1 (
    .in0(register_1_q), .in1(WriteData), .out(multiplexer_1_out), .sel(and_1_out));
  Multiplexer #(.width(8), .enable("false")) multiplexer_2 (
    .in0(register_2_q), .in1(WriteData), .out(multiplexer_2_out), .sel(and_2_out));
  Multiplexer #(.width(8), .enable("false")) multiplexer_3 (
    .in0(register_3_q), .in1(WriteData), .out(multiplexer_3_out), .sel(and_3_out));
  Multiplexer #(.width(8), .enable("false")) multiplexer_4 (
    .in0(register_4_q), .in1(WriteData), .out(multiplexer_4_out), .sel(and_4_out));
  Register register_1 (.D(multiplexer_1_out), .Q(register_1_q), .clk(Clock));  // open: en, clr
  Register register_2 (.D(multiplexer_2_out), .Q(register_2_q), .clk(Clock));  // open: en, clr
  Register register_3 (.D(multiplexer_3_out), .Q(register_3_q), .clk(Clock));  // open: en, clr
  Register register_4 (.D(multiplexer_4_out), .Q(register_4_q), .clk(Clock));  // open: en, clr
  Multiplexer #(.select(2), .width(8), .enable("false")) multiplexer_5 (
    .in0(register_1_q), .in1(register_2_q), .in2(register_3_q), .in3(register_4_q), .out(ReadData1),
    .sel(ReadReg1));
  Multiplexer #(.select(2), .width(8), .enable("false")) multiplexer_6 (
    .in0(register_1_q), .in1(register_2_q), .in2(register_3_q), .in3(register_4_q), .out(ReadData2),
    .sel(ReadReg2));

  // Notes on the sheet:
  //   Register File 8x8-bits
endmodule
