// Logisim project ass5.circ as structural Verilog
module Control (
  input  [1:0] in_1,
  output MemRead,
  output MemWrite,
  output RegWrite,
  output ALUcontrol,
  output MemToReg,
  output RegDst,
  output AluSrc
);

  wire Addi_out;

  and lw (MemRead, ~in_1[1], ~in_1[0]);  // AND_Gate
  and sw (MemWrite, ~in_1[1], in_1[0]);  // AND_Gate
  and Add (RegDst, in_1[1], ~in_1[0]);  // AND_Gate
  and Addi (Addi_out, in_1[0], in_1[1]);
  or or_1 (RegWrite, MemRead, RegDst, Addi_out);
  or or_2 (ALUcontrol, MemRead, MemWrite, RegDst, Addi_out);
  or or_3 (AluSrc, MemRead, MemWrite, Addi_out);

  assign MemToReg = MemRead;
endmodule
